# Fritzing sketch ballmill (saved by Fritzing 0.9.0b)
breadboards: 1

parts:
  Part1 = Arduino Micro (Rev3)
  U1 = RELAY [package=relay-g5q]
  U2 = RELAY [package=relay-g5q]
  Q1 = Basic FET N-Channel [package="TO220 [THT]"]
  U3 = POT [package=pot_alpha_rv16af-20]
  RE1 = Rotary Encoder [package=THT]
  S1 = Round Pushbutton
  S2 = Round Pushbutton
  S3 = SWITCH-MOMENTARY-2 [package=tactile-switch-1101ne]
  Part2 = DeuLigne 1.1 - The Snootlab's LCD shield for Arduino
  VCC1 = 4 x AAA Battery Mount
  VCC2 = 4 x AAA Battery Mount
  M1 = DC Motor

nets:
  GND: Part1.GND, U1.COIL1, U2.COIL1, Q1.drain, U3.E, RE1.EncoderPinC, S1.leg0, S2.leg0, S3.1, Part2.GND, VCC2.-
  N1: Part1.D7, U1.COIL2, U2.COIL2
  N2: Part1.D8_PWM/A8, S3.2
  N3: Part1.D9_PWM/A9, RE1.EncoderPinB
  N4: Part1.D10_PWM/A10, RE1.EncoderPinA
  N5: Part1.D11_PWM, S1.leg1
  N6: Part1.D12_PWM/A11, S2.leg1
  N7: Part1.VIN, U1.MAIN, VCC1.+
  5V: Part1.5V, U3.A, Part2.VIN
  N8: Part1.A5, Part2.A5(CLK)
  N9: Part1.A4, Part2.A4(SDA)
  N10: Part1.A3, Q1.gate
  N11: U1.NO, U2.NC, M1.pin_1
  N12: U1.NC, U2.NO, M1.pin_2
  N13: U2.MAIN, Q1.source
  N14: VCC1.-, VCC2.+
